# Fritzing sketch wiring (saved by Fritzing 0.9.3b)

parts:
  U1 = NodeMCU V3.0
  DHT1 = DHT22 Humidity and Temperature Sensor

nets:
  N1: U1.D0, U1.RST
  3V3: U1.3V3, DHT1.VDD
  N2: U1.D7, DHT1.DATA
  GND: U1.GND, DHT1.GND

custom parts:
  NodeMCU V3.0: ESP8266 based NodeMCU
